# Fritzing sketch PL_Arduino101Ruler (saved by Fritzing 0.9.3b)
breadboards: 1

parts:
  hc-sr1 = hc-sr04
  SG1 = Buzzer 12mm [package=buzzer-12mm-ns]
  R1 = Resistor [tolerance=±1% resistance=1k package=THT]
  Part2 = Arduino 101
  R2 = Trimmer Potentiometer [maximum_resistance=10kΩ package=THT]
  U1 = LCD-16X2 [package=lcd-16x2]

nets:
  VCC: hc-sr1.VCC, Part2.5V
  N1: hc-sr1.Trig, Part2.D7
  N2: hc-sr1.Echo, R1.Pin_0
  GND: hc-sr1.GND, SG1.2, Part2.GND, R2.leg2, U1.VSS, U1.K
  N3: SG1.1, Part2.D9_PWM
  N4: R1.Pin_1, Part2.D6_PWM
  N5: Part2.D11_PWM/MOSI, U1.R_W
  N6: Part2.D12/MISO, U1.RS
  N7: Part2.D2, U1.DB7
  N8: Part2.D3_PWM, U1.DB6
  N9: Part2.D4, U1.DB5
  N10: Part2.D5_PWM, U1.DB4
  3V3: Part2.3V3, R2.leg1, U1.VDD, U1.A
  N11: R2.wiper, U1.VO

custom parts:
  Arduino 101: A learning and development board that delivers the performance and low-power consumption of the Intel® Curie™ Module with the simplicity of Arduino at an entry-level price. It keeps the same robust form factor and peripheral list of the UNO with the addition of onboard Bluetooth LE capabilities and a 6-axis accelerometer/gyro to help you easily expand your creativity into the connected world.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
